# Fritzing sketch Switchy_graph (saved by Fritzing 0.9.3b)
breadboards: 1

parts:
  R1 = 330 Ω Resistor [package=THT]
  R2 = 330 Ω Resistor [package=THT]
  R3 = 330 Ω Resistor [package=THT]
  R6 = 330 Ω Resistor [package=THT]
  White = LED - 5mm [color="White (6500K)" package="5 mm [THT]"]
  Yellow = LED - 5mm [color="Yellow (595nm)" package="5 mm [THT]"]
  Red = LED - 5mm [color="Red (633nm)" package="5 mm [THT]"]
  Blue = LED - 5mm [color="Blue (525nm)" package="5 mm [THT]"]
  Green = LED - 5mm [color="Green (570nm)" package="5 mm [THT]"]
  Snow = LED - 5mm [color="White (6500K)" package="5 mm [THT]"]
  R4 = 330 Ω Resistor [package=THT]
  R5 = 330 Ω Resistor [package=THT]
  Raspberry_Pi_1 = Raspberry Pi 3 [part_number=RPI-3-V1.2]

nets:
  N1: R1.Pin_0, R2.Pin_0, R3.Pin_0, R6.Pin_0, R4.Pin_0, R5.Pin_0, Raspberry_Pi_1.GPIO10, Raspberry_Pi_1.GND
  N2: R1.Pin_1, White.cathode
  N3: R2.Pin_1, Yellow.cathode
  N4: R3.Pin_1, Red.cathode
  N5: R6.Pin_1, Snow.cathode
  N6: White.anode, Raspberry_Pi_1.GPIO21
  N7: Yellow.anode, Raspberry_Pi_1.GPIO19, Raspberry_Pi_1.GPIO16
  N8: Red.anode, Raspberry_Pi_1.GPIO6, Raspberry_Pi_1.GPIO12
  N9: Blue.cathode, R4.Pin_1
  N10: Blue.anode, Raspberry_Pi_1.GPIO9, Raspberry_Pi_1.GPIO25
  N11: Green.cathode, R5.Pin_1
  N12: Green.anode, Raspberry_Pi_1.3V3, Raspberry_Pi_1.GPIO24
  N13: Snow.anode, Raspberry_Pi_1.GPIO22, Raspberry_Pi_1.GPIO23

custom parts:
  330 Ω Resistor: A generic 5-band resistor (0.25W)
